# Fritzing sketch Capstone_BPWCB (saved by Fritzing 0.8.7b)

parts:
  U1 = NEO 6M GPS
  Part1 = Arduino Mega 2560 (Rev3)
  Part2 = Adafruit FONA - Mini Cellular GSM Breakout
  Keyes1 = Keyes IR Infrared Sensor Switch Module
  U3 = HC-SR04 [chip_label=IC package="SIP (Single Inline) [THT]"]
  S1 = H-Bridge with L298N
  S2 = H-Bridge with L298N
  M1 = DC Motor
  M2 = DC Motor
  M3 = DC Motor
  J1 = Basic Servo

nets:
  N1: U1.RXD, Part1.D1_TX0
  N2: U1.TXD, Part1.D0_RX0
  GND: U1.GND, Part1.GND, Part2.GND, Keyes1.GND, U3.GND, J1.gnd
  VCC: U1.VCC, Part1.5V, Part2.VBAT, Keyes1.VCC, U3.Vcc, J1.vcc
  N3: Part1.D19/RX1, Part2.TXD_5V
  N4: Part1.D18/TX1, Part2.RXD_5V
  5V: Part1.VIN, S1.5V, S2.5V
  N5: Part1.D2_PWM, U3.Echo
  N6: Part1.D3_PWM, U3.Trig
  N7: Part1.D4_PWM, J1.pulse
  N8: Part1.D5_PWM, S2.ENA
  N9: Part1.D6_PWM, S1.ENA
  N10: Part1.D7_PWM, S1.ENB
  N11: Part1.D22, Keyes1.EN
  N12: Part1.D23, Keyes1.out
  N13: S1.M1-01, M2.pin_2
  N14: S1.M1-02, M2.pin_1
  N15: S1.M2-01, M1.pin_2
  N16: S1.M2-02, M1.pin_1
  N17: S2.M1-01, M3.pin_2
  N18: S2.M1-02, M3.pin_1

custom parts:
  NEO 6M GPS: uSD module
  Adafruit FONA - Mini Cellular GSM Breakout: An all-in-one cellular phone module that lets you add voice, text, SMS and GPRS data to your project. Quad-band 850/900/1800/1900MHz - connect onto any global GSM network with any 2G SIM. Includes an onboard LiPoly battery charging circuitry so you can take your project on the go. Also works as an FM radio receiver.
  Keyes IR Infrared Sensor Switch Module: An infrared obstacle detector
  HC-SR04: HC-SR04 ultrasound distance sensor
  H-Bridge with L298N: h-bridge
